// Logisim project 4  Bit Full Adder Circuit.circ as structural Verilog: 1 circuit, main circuit main
module main (
  input  A0,
  input  B0,
  input  Cin,
  input  A1,
  input  B1,
  input  C1,
  input  A2,
  input  B2,
  input  A3,
  input  C2,
  input  B3,
  input  C3,
  output Sum_0,
  output Sum_1,
  output Sum_2,
  output Sum_3,
  output Cout
);

  wire and_1_out, and_2_out, and_3_out, and_4_out, and_5_out, and_6_out, and_7_out, and_8_out, or_1_out,
       or_2_out, or_3_out, xor_1_out, xor_3_out, xor_5_out, xor_7_out;

  xor xor_1 (xor_1_out, A0, B0);
  xor xor_2 (Sum_0, xor_1_out, Cin);
  and and_1 (and_1_out, Cin, xor_1_out);
  and and_2 (and_2_out, B0, A0);
  or or_1 (or_1_out, and_1_out, and_2_out);
  xor xor_3 (xor_3_out, A1, B1);
  xor xor_4 (Sum_1, xor_3_out, C1);
  and and_3 (and_3_out, C1, xor_3_out);
  and and_4 (and_4_out, B1, A1);
  or or_2 (or_2_out, and_3_out, and_4_out);
  xor xor_5 (xor_5_out, A2, B2);
  xor xor_6 (Sum_2, xor_5_out, C2);
  and and_5 (and_5_out, C2, xor_5_out);
  and and_6 (and_6_out, B2, A2);
  or or_3 (or_3_out, and_5_out, and_6_out);
  xor xor_7 (xor_7_out, A3, B3);
  xor xor_8 (Sum_3, xor_7_out, C3);
  and and_7 (and_7_out, C3, xor_7_out);
  and and_8 (and_8_out, B3, A3);
  or or_4 (Cout, and_7_out, and_8_out);
endmodule
