// Logisim project 4 Bit Full Adder Circuit (Simpler).circ as structural Verilog: 2 circuits, main circuit 1 Bit Full Adder
module _1_Bit_Full_Adder (
  input  A,
  input  B,
  input  Cin,
  output Sum,
  output Cout
);

  wire and_1_out, and_2_out, xor_1_out;

  and and_1 (and_1_out, A, B);
  xor xor_1 (xor_1_out, A, B);
  and and_2 (and_2_out, xor_1_out, Cin);
  xor xor_2 (Sum, xor_1_out, Cin);
  or or_1 (Cout, and_2_out, and_1_out);
endmodule

module _4_Bit_Full_Adder (
  input  Cin,
  input  [3:0] A3_A2_A1_A0,
  input  [3:0] B3_B2_B1_B0,
  output [3:0] S3_S2_S1_S0,
  output Cout
);

  wire n1_bit_full_adder_1_cout, n1_bit_full_adder_2_cout, n1_bit_full_adder_3_cout;

  _1_Bit_Full_Adder u_1_bit_full_adder_1 (
    .A(A3_A2_A1_A0[0]), .B(B3_B2_B1_B0[0]), .Cin(Cin), .Sum(S3_S2_S1_S0[0]), .Cout(n1_bit_full_adder_1_cout));
  _1_Bit_Full_Adder u_1_bit_full_adder_2 (
    .A(A3_A2_A1_A0[1]), .B(B3_B2_B1_B0[1]), .Cin(n1_bit_full_adder_1_cout), .Sum(S3_S2_S1_S0[1]),
    .Cout(n1_bit_full_adder_2_cout));
  _1_Bit_Full_Adder u_1_bit_full_adder_3 (
    .A(A3_A2_A1_A0[2]), .B(B3_B2_B1_B0[2]), .Cin(n1_bit_full_adder_2_cout), .Sum(S3_S2_S1_S0[2]),
    .Cout(n1_bit_full_adder_3_cout));
  _1_Bit_Full_Adder u_1_bit_full_adder_4 (
    .A(A3_A2_A1_A0[3]), .B(B3_B2_B1_B0[3]), .Cin(n1_bit_full_adder_3_cout), .Sum(S3_S2_S1_S0[3]), .Cout(Cout));
endmodule
