// Logisim project T-Flipflop.circ as structural Verilog: 1 circuit, main circuit main
module main (
  input  T,
  output Q,
  output Q_Bar
);

  wire and_1_out, and_2_out, Clk_out, nand_1_out, nand_2_out;

  and and_1 (and_1_out, Q_Bar, T);
  and and_2 (and_2_out, T, Q);
  Clock Clk (.out(Clk_out));
  nand nand_1 (nand_1_out, and_1_out, Clk_out);
  nand nand_2 (nand_2_out, Clk_out, and_2_out);
  nand nand_3 (Q, nand_1_out, Q_Bar);
  nand nand_4 (Q_Bar, Q, nand_2_out);
endmodule
